// Logisim project WITCPU.circ as structural Verilog: 4 circuits, main circuit register_group
module register_group (
  input  [15:0] in_1,
  input  Clock,
  input  [1:0] Ra,
  input  [1:0] Rd,
  input  [1:0] Rb,
  output [15:0] Ra_output,
  output [15:0] Rb_output
);

  wire demultiplexer_1_out0, demultiplexer_1_out1, demultiplexer_1_out2, demultiplexer_1_out3;
  wire [15:0] register_1_q, register_2_q, register_3_q, register_4_q;

  Demultiplexer #(.select(2)) demultiplexer_1 (
    .out0(demultiplexer_1_out0), .out1(demultiplexer_1_out1), .out2(demultiplexer_1_out2),
    .out3(demultiplexer_1_out3), .in(Clock), .sel(Rd));  // open: en
  Register #(.width(16)) register_1 (.D(in_1), .Q(register_1_q), .clk(demultiplexer_1_out0));  // open: en, clr
  Register #(.width(16)) register_2 (.D(in_1), .Q(register_2_q), .clk(demultiplexer_1_out1));  // open: en, clr
  Register #(.width(16)) register_3 (.D(in_1), .Q(register_3_q), .clk(demultiplexer_1_out2));  // open: en, clr
  Register #(.width(16)) register_4 (.D(in_1), .Q(register_4_q), .clk(demultiplexer_1_out3));  // open: en, clr
  Multiplexer #(.select(2), .width(16)) multiplexer_1 (
    .in0(register_1_q), .in1(register_2_q), .in2(register_3_q), .in3(register_4_q), .out(Ra_output), .sel(Ra));  // open: en
  Multiplexer #(.select(2), .width(16)) multiplexer_2 (
    .in0(register_1_q), .in1(register_2_q), .in2(register_3_q), .in3(register_4_q), .out(Rb_output), .sel(Rb));  // open: en
endmodule

module registers (
  input  [15:0] Rd_value,
  input  clock,
  input  [3:0] Rd,
  input  [1:0] Rx,
  input  [1:0] Ry,
  output [15:0] Rx_output,
  output [15:0] Ry_output
);

  wire demultiplexer_1_out0, demultiplexer_1_out1, demultiplexer_1_out2, demultiplexer_1_out3;
  wire [15:0] R0___R3_ra_output, R0___R3_rb_output, R4___R7_ra_output, R4___R7_rb_output, R8___Rb_ra_output,
       R8___Rb_rb_output, Rc___Rf_ra_output, Rc___Rf_rb_output;

  Demultiplexer #(.select(2)) demultiplexer_1 (
    .out0(demultiplexer_1_out0), .out1(demultiplexer_1_out1), .out2(demultiplexer_1_out2),
    .out3(demultiplexer_1_out3), .in(clock), .sel(Rd[1:0]));  // open: en
  register_group_with_r0 R0___R3 (
    .in_1(Rd_value), .Clock(demultiplexer_1_out0), .Ra(Rx), .Rd(Rd[3:2]), .Rb(Ry),
    .Ra_output(R0___R3_ra_output), .Rb_output(R0___R3_rb_output));
  register_group R4___R7 (
    .in_1(Rd_value), .Clock(demultiplexer_1_out1), .Ra(Rx), .Rd(Rd[3:2]), .Rb(Ry),
    .Ra_output(R4___R7_ra_output), .Rb_output(R4___R7_rb_output));
  register_group R8___Rb (
    .in_1(Rd_value), .Clock(demultiplexer_1_out2), .Ra(Rx), .Rd(Rd[3:2]), .Rb(Ry),
    .Ra_output(R8___Rb_ra_output), .Rb_output(R8___Rb_rb_output));
  register_group Rc___Rf (
    .in_1(Rd_value), .Clock(demultiplexer_1_out3), .Ra(Rx), .Rd(Rd[3:2]), .Rb(Ry),
    .Ra_output(Rc___Rf_ra_output), .Rb_output(Rc___Rf_rb_output));
  Multiplexer #(.select(2), .width(16)) multiplexer_1 (
    .in0(R0___R3_ra_output), .in1(R4___R7_ra_output), .in2(R8___Rb_ra_output), .in3(Rc___Rf_ra_output),
    .out(Rx_output), .sel(Rd[1:0]));  // open: en
  Multiplexer #(.select(2), .width(16)) multiplexer_2 (
    .in0(R0___R3_rb_output), .in1(R4___R7_rb_output), .in2(R8___Rb_rb_output), .in3(Rc___Rf_rb_output),
    .out(Ry_output), .sel(Rd[1:0]));  // open: en
endmodule

module register_group_with_r0 (
  input  [15:0] in_1,
  input  Clock,
  input  [1:0] Ra,
  input  [1:0] Rd,
  input  [1:0] Rb,
  output [15:0] Ra_output,
  output [15:0] Rb_output
);

  wire demultiplexer_1_out0, demultiplexer_1_out1, demultiplexer_1_out2, demultiplexer_1_out3;
  wire [15:0] register_1_q, register_2_q, register_3_q, register_4_q;

  Demultiplexer #(.select(2)) demultiplexer_1 (
    .out0(demultiplexer_1_out0), .out1(demultiplexer_1_out1), .out2(demultiplexer_1_out2),
    .out3(demultiplexer_1_out3), .in(Clock), .sel(Rd));  // open: en
  Register #(.width(16)) register_1 (.D({16{1'b0}}), .Q(register_1_q), .clk(demultiplexer_1_out0));  // open: en, clr
  Register #(.width(16)) register_2 (.D(in_1), .Q(register_2_q), .clk(demultiplexer_1_out1));  // open: en, clr
  Register #(.width(16)) register_3 (.D(in_1), .Q(register_3_q), .clk(demultiplexer_1_out2));  // open: en, clr
  Register #(.width(16)) register_4 (.D(in_1), .Q(register_4_q), .clk(demultiplexer_1_out3));  // open: en, clr
  Multiplexer #(.select(2), .width(16)) multiplexer_1 (
    .in0(register_1_q), .in1(register_2_q), .in2(register_3_q), .in3(register_4_q), .out(Ra_output), .sel(Ra));  // open: en
  Multiplexer #(.select(2), .width(16)) multiplexer_2 (
    .in0(register_1_q), .in1(register_2_q), .in2(register_3_q), .in3(register_4_q), .out(Rb_output), .sel(Rb));  // open: en
endmodule

module test (
  input  [15:0] in_1,
  input  [3:0] in_2,
  input  [1:0] in_3,
  input  [1:0] in_4,
  output [15:0] out_5,
  output [15:0] out_6
);

  wire clock_1_out;

  Clock clock_1 (.out(clock_1_out));
  registers registers_1 (
    .Rd_value(in_1), .clock(clock_1_out), .Rd(in_2), .Rx(in_3), .Ry(in_4), .Rx_output(out_5),
    .Ry_output(out_6));
endmodule
